# Fritzing sketch flip_flop (saved by Fritzing 0.9.1b)
circuit board: 6.98975cm x 5.79875cm
breadboards: 1

parts:
  S1 = Pushbutton [package="[THT]"]
  R1 = Resistor [tolerance=±5% resistance=10k package=THT]
  R2 = Resistor [tolerance=±5% resistance=330 package=THT]
  R3 = Resistor [tolerance=±5% resistance=330 package=THT]
  LED1 = LED - 5mm [color="Red (633nm)" package="5 mm [THT]"]
  LED2 = LED - 5mm [color="Green (555nm)" package="5 mm [THT]"]
  Shield_FLIP-FLOP = Arduino Uno (Rev3)

nets:
  N1: S1.Pin_1, S1.Pin_2, R1.Pin_0, Shield_FLIP-FLOP.D2
  N2: S1.Pin_3, S1.Pin_4, Shield_FLIP-FLOP.5V
  N3: R1.Pin_1, LED1.cathode, LED2.cathode, Shield_FLIP-FLOP.GND
  N4: R2.Pin_0, Shield_FLIP-FLOP.D8
  N5: R2.Pin_1, LED1.anode
  N6: R3.Pin_0, Shield_FLIP-FLOP.D7
  N7: R3.Pin_1, LED2.anode

notes:
  http://moncoursdetechno.free.fr

// code stored in the sketch: flip-flop.ino
// programme test pour câblage FLIP-FLOP
// BP sur entrée numérique n°2
// Del rouge sur sortie numérique n° 8
// Del verte sur sortie numérique n° 7

void setup()
{
  pinMode( 13 , OUTPUT);
  pinMode( 12 , OUTPUT);
}

void loop()
{
  digitalWrite( 13 , HIGH );
  digitalWrite( 12 , LOW );
  delay( 3000 );
  digitalWrite( 13 , LOW );
  digitalWrite( 12 , HIGH );
  delay( 3000 );
}

//laurent Chastain
//académie de LIMOGES
//http://moncoursdetechno.free.fr
